// Logisim project Control_PLA_sim.circ as structural Verilog: 1 circuit, main circuit main
module main (
  input  Op_0,
  input  Op_1,
  input  Op_2,
  input  Op_3,
  input  Op_4,
  input  Op_5,
  output RegDst,
  output AluSrc,
  output MemToReg,
  output RegWrite,
  output MemRead,
  output MemWrite,
  output ALU_op_0,
  output ALU_op_1,
  output beq,
  output bne,
  output bgtz
);

  wire ADDI_out, LW_out, not_1_out, not_2_out, not_3_out, not_4_out, not_5_out, not_6_out;

  not not_1 (not_1_out, Op_0);
  not not_2 (not_2_out, Op_1);
  not not_3 (not_3_out, Op_2);
  not not_4 (not_4_out, Op_3);
  not not_5 (not_5_out, Op_4);
  not not_6 (not_6_out, Op_5);
  and R_format (ALU_op_1, not_1_out, not_2_out, not_3_out, not_4_out, not_5_out, not_6_out);
  and ADDI (ADDI_out, not_1_out, not_2_out, not_3_out, Op_3, not_5_out, not_6_out);
  and LW (LW_out, Op_0, Op_1, not_3_out, not_4_out, not_5_out, Op_5);
  and SW (MemWrite, Op_0, Op_1, not_3_out, Op_3, not_5_out, Op_5);
  and u_BEQ (beq, not_1_out, not_2_out, Op_2, not_4_out, not_5_out, not_6_out);
  and u_BNE (bne, Op_0, not_2_out, Op_2, not_4_out, not_5_out, not_6_out);
  and u_BGTZ (bgtz, Op_0, Op_1, Op_2, not_4_out, not_5_out, not_6_out);
  or or_1 (AluSrc, ADDI_out, LW_out, MemWrite);
  buf or_2 (MemToReg, LW_out);  // OR_Gate
  or or_3 (RegWrite, ALU_op_1, ADDI_out, LW_out);
  or or_4 (MemRead, LW_out, MemWrite);
  or or_5 (ALU_op_0, beq, bne, bgtz);

  assign RegDst = ALU_op_1;
endmodule
